// Digital circuit 1bitRegister.dig as structural Verilog
module _1bitRegister (
  input  I,
  input  S,
  input  P,
  output D
);

  wire and_1_out, and_2_out, not_1_out, or_1_out;

  not not_1 (not_1_out, S);
  and and_1 (and_1_out, D, not_1_out);
  and and_2 (and_2_out, I, S);
  or or_1 (or_1_out, and_1_out, and_2_out);
  dataFlipFlop dataflipflop_1 (.I(or_1_out), .P(P), .D(D));
endmodule
