// Digital circuit 8bitAdder.dig as structural Verilog
module _8bitAdder (
  input  A7,
  input  A6,
  input  A5,
  input  A4,
  input  A3,
  input  A2,
  input  A1,
  input  A0,
  input  B7,
  input  B6,
  input  B5,
  input  B4,
  input  B3,
  input  B2,
  input  B1,
  input  B0,
  input  Ci,
  output R7,
  output R6,
  output R5,
  output R4,
  output R3,
  output R2,
  output R1,
  output R0,
  output Co
);

  wire adder_1_co, adder_2_co, adder_3_co, adder_4_co, adder_5_co, adder_6_co, adder_7_co;

  adder adder_1 (.A(A0), .B(B0), .Ci(Ci), .R(R0), .Co(adder_1_co));
  adder adder_2 (.A(A1), .B(B1), .Ci(adder_1_co), .R(R1), .Co(adder_2_co));
  adder adder_3 (.A(A2), .B(B2), .Ci(adder_2_co), .R(R2), .Co(adder_3_co));
  adder adder_4 (.A(A3), .B(B3), .Ci(adder_3_co), .R(R3), .Co(adder_4_co));
  adder adder_5 (.A(A4), .B(B4), .Ci(adder_4_co), .R(R4), .Co(adder_5_co));
  adder adder_6 (.A(A5), .B(B5), .Ci(adder_5_co), .R(R5), .Co(adder_6_co));
  adder adder_7 (.A(A6), .B(B6), .Ci(adder_6_co), .R(R6), .Co(adder_7_co));
  adder adder_8 (.A(A7), .B(B7), .Ci(adder_7_co), .R(R7), .Co(Co));
endmodule
