// Digital circuit 8bitAdderSubstractor.dig as structural Verilog
module _8bitAdderSubstractor (
  input  A7,
  input  A6,
  input  A5,
  input  A4,
  input  A3,
  input  A2,
  input  A1,
  input  A0,
  input  B7,
  input  B6,
  input  B5,
  input  B4,
  input  B3,
  input  B2,
  input  B1,
  input  B0,
  input  S,
  input  Ci,
  output O7,
  output O6,
  output O5,
  output O4,
  output O3,
  output O2,
  output O1,
  output O0,
  output Co
);

  wire inverter_1_o0, inverter_1_o1, inverter_1_o2, inverter_1_o3, inverter_1_o4, inverter_1_o5,
       inverter_1_o6, inverter_1_o7, xor_1_out;

  xor xor_1 (xor_1_out, S, Ci);
  inverter inverter_1 (
    .A7(B7), .A6(B6), .A5(B5), .A4(B4), .A3(B3), .A2(B2), .A1(B1), .A0(B0), .B(S), .O7(inverter_1_o7),
    .O6(inverter_1_o6), .O5(inverter_1_o5), .O4(inverter_1_o4), .O3(inverter_1_o3), .O2(inverter_1_o2),
    .O1(inverter_1_o1), .O0(inverter_1_o0));
  _8bitAdder _8bitadder_1 (
    .A7(A7), .A6(A6), .A5(A5), .A4(A4), .A3(A3), .A2(A2), .A1(A1), .A0(A0), .B7(inverter_1_o7),
    .B6(inverter_1_o6), .B5(inverter_1_o5), .B4(inverter_1_o4), .B3(inverter_1_o3), .B2(inverter_1_o2),
    .B1(inverter_1_o1), .B0(inverter_1_o0), .Ci(xor_1_out), .R7(O7), .R6(O6), .R5(O5), .R4(O4), .R3(O3),
    .R2(O2), .R1(O1), .R0(O0), .Co(Co));
endmodule
