// Digital circuit 8bitRegister.dig as structural Verilog
module _8bitRegister (
  input  I7,
  input  I6,
  input  I5,
  input  I4,
  input  I3,
  input  I2,
  input  I1,
  input  I0,
  input  S,
  input  P,
  output D7,
  output D6,
  output D5,
  output D4,
  output D3,
  output D2,
  output D1,
  output D0
);

  _1bitRegister _1bitregister_1 (.I(I7), .S(S), .P(P), .D(D7));
  _1bitRegister _1bitregister_2 (.I(I6), .S(S), .P(P), .D(D6));
  _1bitRegister _1bitregister_3 (.I(I5), .S(S), .P(P), .D(D5));
  _1bitRegister _1bitregister_4 (.I(I4), .S(S), .P(P), .D(D4));
  _1bitRegister _1bitregister_5 (.I(I3), .S(S), .P(P), .D(D3));
  _1bitRegister _1bitregister_6 (.I(I2), .S(S), .P(P), .D(D2));
  _1bitRegister _1bitregister_7 (.I(I1), .S(S), .P(P), .D(D1));
  _1bitRegister _1bitregister_8 (.I(I0), .S(S), .P(P), .D(D0));
endmodule
