// Digital circuit 8bitSubtractor.dig as structural Verilog
module _8bitSubtractor (
  input  A7,
  input  A6,
  input  A5,
  input  A4,
  input  A3,
  input  A2,
  input  A1,
  input  A0,
  input  B7,
  input  B6,
  input  B5,
  input  B4,
  input  B3,
  input  B2,
  input  B1,
  input  B0,
  input  Bi,
  output R0,
  output R1,
  output R2,
  output R3,
  output R4,
  output R5,
  output R6,
  output R7,
  output Bo
);

  wire subtractor_1_bo, subtractor_2_bo, subtractor_3_bo, subtractor_4_bo, subtractor_5_bo, subtractor_6_bo,
       subtractor_7_bo;

  subtractor subtractor_1 (.A(A0), .B(B0), .Bi(Bi), .R(R0), .Bo(subtractor_1_bo));
  subtractor subtractor_2 (.A(A1), .B(B1), .Bi(subtractor_1_bo), .R(R1), .Bo(subtractor_2_bo));
  subtractor subtractor_3 (.A(A2), .B(B2), .Bi(subtractor_2_bo), .R(R2), .Bo(subtractor_3_bo));
  subtractor subtractor_4 (.A(A3), .B(B3), .Bi(subtractor_3_bo), .R(R3), .Bo(subtractor_4_bo));
  subtractor subtractor_5 (.A(A4), .B(B4), .Bi(subtractor_4_bo), .R(R4), .Bo(subtractor_5_bo));
  subtractor subtractor_6 (.A(A5), .B(B5), .Bi(subtractor_5_bo), .R(R5), .Bo(subtractor_6_bo));
  subtractor subtractor_7 (.A(A6), .B(B6), .Bi(subtractor_6_bo), .R(R6), .Bo(subtractor_7_bo));
  subtractor subtractor_8 (.A(A7), .B(B7), .Bi(subtractor_7_bo), .R(R7), .Bo(Bo));
endmodule
