// Digital circuit arithmetic&logic.dig as structural Verilog
module arithmetic_logic (
  input  A7,
  input  A6,
  input  A5,
  input  A4,
  input  A3,
  input  A2,
  input  A1,
  input  A0,
  input  B7,
  input  B6,
  input  B5,
  input  B4,
  input  B3,
  input  B2,
  input  B1,
  input  B0,
  input  S,
  input  Ci,
  output O7,
  output O6,
  output O5,
  output O4,
  output O3,
  output O2,
  output O1,
  output O0,
  output Co,
  output N,
  output Z
);

  wire not_1_out, not_2_out, not_3_out, not_4_out, not_5_out, not_6_out, not_7_out, not_8_out;

  _8bitAdderSubstractor _8bitaddersubstractor_1 (
    .A7(A7), .A6(A6), .A5(A5), .A4(A4), .A3(A3), .A2(A2), .A1(A1), .A0(A0), .B7(B7), .B6(B6), .B5(B5),
    .B4(B4), .B3(B3), .B2(B2), .B1(B1), .B0(B0), .S(S), .Ci(Ci), .O7(N), .O6(O6), .O5(O5), .O4(O4), .O3(O3),
    .O2(O2), .O1(O1), .O0(O0), .Co(Co));
  not not_1 (not_1_out, N);
  not not_2 (not_2_out, O6);
  not not_3 (not_3_out, O5);
  not not_4 (not_4_out, O4);
  not not_5 (not_5_out, O3);
  not not_6 (not_6_out, O2);
  not not_7 (not_7_out, O1);
  not not_8 (not_8_out, O0);
  and and_1 (Z, not_1_out, not_2_out, not_3_out, not_4_out, not_5_out, not_6_out, not_7_out, not_8_out);

  assign O7 = N;
endmodule
