// Digital circuit cpu.dig as structural Verilog
module cpu (
  input  I7,
  input  I6,
  input  I5,
  input  I4,
  input  I3,
  input  I2,
  input  I1,
  input  I0,
  input  P,
  input  C_2,
  output O7,
  output O6,
  output O5,
  output O4,
  output O3,
  output O2,
  output O1,
  output O0,
  output Z,
  output C
);

  wire _1bitregister_1_d, _1bitregister_2_d, _8bitregister_1_d0, _8bitregister_1_d1, _8bitregister_1_d2,
       _8bitregister_1_d3, _8bitregister_1_d4, _8bitregister_1_d5, _8bitregister_1_d6, _8bitregister_1_d7,
       _8bitregister_2_p12, _8bitregister_2_p13, _8bitregister_2_p14, _8bitregister_2_p15,
       _8bitregister_2_p16, _8bitregister_2_p17, _8bitregister_2_p18, _8bitregister_2_p19, and_1_out,
       and_2_out, arithmetic_logic_1_co, dataflipflop_1_d, not_1_out;

  _1bitRegister _1bitregister_1 (.I(I1), .S(C_2), .P(P), .D(_1bitregister_1_d));
  _1bitRegister _1bitregister_2 (.I(I0), .S(C_2), .P(P), .D(_1bitregister_2_d));
  and and_1 (and_1_out, _1bitregister_2_d, ~_1bitregister_1_d);  // And
  and and_2 (and_2_out, _1bitregister_2_d, _1bitregister_1_d);
  _8bitRegister _8bitregister_1 (
    .I7(I7), .I6(I6), .I5(I5), .I4(I4), .I3(I3), .I2(I2), .I1(I1), .I0(I0), .S(and_1_out), .P(P),
    .D7(_8bitregister_1_d7), .D6(_8bitregister_1_d6), .D5(_8bitregister_1_d5), .D4(_8bitregister_1_d4),
    .D3(_8bitregister_1_d3), .D2(_8bitregister_1_d2), .D1(_8bitregister_1_d1), .D0(_8bitregister_1_d0));
  // _8bitRegister _8bitregister_2: pin names not known; wires that end beside it: I7, I6, I5, I4, I3, I2, I1, I0, and_2_out, P, _8bitregister_1_d0, _8bitregister_2_p12, _8bitregister_2_p13, _8bitregister_2_p14, _8bitregister_2_p15, _8bitregister_2_p16, _8bitregister_2_p17, _8bitregister_2_p18, _8bitregister_2_p19
  not not_1 (not_1_out, _1bitregister_2_d);
  arithmetic_logic arithmetic_logic_1 (
    .A7(_8bitregister_1_d7), .A6(_8bitregister_1_d6), .A5(_8bitregister_1_d5), .A4(_8bitregister_1_d4),
    .A3(_8bitregister_1_d3), .A2(_8bitregister_1_d2), .A1(_8bitregister_1_d1), .A0(_8bitregister_1_d0),
    .B7(_8bitregister_2_p12), .B6(_8bitregister_2_p13), .B5(_8bitregister_2_p14), .B4(_8bitregister_2_p15),
    .B3(_8bitregister_2_p16), .B2(_8bitregister_2_p17), .B1(_8bitregister_2_p18), .B0(_8bitregister_2_p19),
    .S(not_1_out), .Ci(dataflipflop_1_d), .O7(O7), .O6(O6), .O5(O5), .O4(O4), .O3(O3), .O2(O2), .O1(O1),
    .O0(O0), .Co(arithmetic_logic_1_co), .Z(Z));
  dataFlipFlop dataflipflop_1 (.I(C), .P(P), .D(dataflipflop_1_d));
  and and_3 (C, arithmetic_logic_1_co, ~not_1_out);  // And
endmodule
