// Digital circuit dataFlipFlop.dig as structural Verilog
module dataFlipFlop (
  input  I,
  input  P,
  output D
);

  wire datalatch_1_d, not_1_out;

  not not_1 (not_1_out, P);
  dataLatch datalatch_1 (.I(I), .S(not_1_out), .D(datalatch_1_d));
  dataLatch datalatch_2 (.I(datalatch_1_d), .S(P), .D(D));
endmodule
