// Digital circuit dataLatch.dig as structural Verilog
module dataLatch (
  input  I,
  input  S,
  output D
);

  wire and_1_out, and_2_out, nor_1_out, not_1_out;

  not not_1 (not_1_out, I);
  and and_1 (and_1_out, I, S);
  and and_2 (and_2_out, S, not_1_out);
  nor nor_1 (nor_1_out, and_1_out, D);
  nor nor_2 (D, nor_1_out, and_2_out);
endmodule
