// Digital circuit inverter.dig as structural Verilog
module inverter (
  input  A7,
  input  A6,
  input  A5,
  input  A4,
  input  A3,
  input  A2,
  input  A1,
  input  A0,
  input  B,
  output O7,
  output O6,
  output O5,
  output O4,
  output O3,
  output O2,
  output O1,
  output O0
);

  xor xor_1 (O7, A7, B);
  xor xor_2 (O6, A6, B);
  xor xor_3 (O5, A5, B);
  xor xor_4 (O4, A4, B);
  xor xor_5 (O3, A3, B);
  xor xor_6 (O2, A2, B);
  xor xor_7 (O1, A1, B);
  xor xor_8 (O0, A0, B);
endmodule
